// Logisim project Project.circ as structural Verilog: 1 circuit, main circuit main
module main (
  input  [7:0] Starting_Address,
  output [7:0] out_2
);

  wire CLK, decoder_1_out0, decoder_1_out1, decoder_1_out2, decoder_1_out3, EN, EndLED, even_parity_1_out,
       j_k_ff_1_q, not_1_out, not_2_out, odd_parity_1_out, RUN_out, Rx, xor_1_out;
  wire [1:0] Rd, Rs;
  wire [2:0] OPCODE, R2_q_2, R3_q_2, R4_q_2;
  wire [3:0] bit_extender_1_out, bit_extender_2_out, bit_extender_3_out, bit_extender_4_out, R2_q, R3_q, R4_q;
  wire [6:0] adder_1_out, IMM, multiplexer_1_out, multiplexer_2_out, multiplexer_3_out, R1_q, shifter_1_out,
       shifter_2_out, subtractor_1_out;
  wire [7:0] bit_extender_5_out, bit_extender_6_out, multiplexer_4_out, Program_Counter_q;

  Decoder #(.select(2)) decoder_1 (
    .out0(decoder_1_out0), .out1(decoder_1_out1), .out2(decoder_1_out2), .out3(decoder_1_out3), .sel(Rd),
    .en(EN));
  Button RUN (.out(RUN_out));
  J_K_Flip_Flop j_k_ff_1 (.J(RUN_out), .K(1'b0), .clk(CLK), .Q(j_k_ff_1_q));  // open: Qn, preset, reset
  Clock clock_1 (.out(CLK));
  Register #(.width(7)) R1 (.D(multiplexer_3_out), .en(decoder_1_out0), .clk(CLK), .Q(R1_q));  // open: clr
  Register #(.width(7)) R2 (.D(multiplexer_3_out), .en(decoder_1_out1), .clk(CLK), .Q({R2_q_2, R2_q}));  // open: clr
  Register #(.width(7)) R3 (.D(multiplexer_3_out), .en(decoder_1_out2), .clk(CLK), .Q({R3_q_2, R3_q}));  // open: clr
  Register #(.width(7)) R4 (.D(multiplexer_3_out), .en(decoder_1_out3), .clk(CLK), .Q({R4_q_2, R4_q}));  // open: clr
  Register u_Rx (.D(multiplexer_4_out), .en(Rx), .clk(CLK), .Q(out_2));  // open: clr
  Hex_Digit_Display hex_digit_display_1 (.value(bit_extender_1_out));  // open: dp
  Hex_Digit_Display #(.decimalPoint("false")) hex_digit_display_2 (.value(R1_q[3:0]));
  assign bit_extender_1_out = {{1{1'b0}}, R1_q[6:4]};  // Bit_Extender bit_extender_1
  Hex_Digit_Display hex_digit_display_3 (.value(bit_extender_2_out));  // open: dp
  Hex_Digit_Display #(.decimalPoint("false")) hex_digit_display_4 (.value(R2_q));
  assign bit_extender_2_out = {{1{1'b0}}, R2_q_2};  // Bit_Extender bit_extender_2
  Hex_Digit_Display hex_digit_display_5 (.value(bit_extender_3_out));  // open: dp
  Hex_Digit_Display #(.decimalPoint("false")) hex_digit_display_6 (.value(R3_q));
  assign bit_extender_3_out = {{1{1'b0}}, R3_q_2};  // Bit_Extender bit_extender_3
  Hex_Digit_Display hex_digit_display_7 (.value(bit_extender_4_out));  // open: dp
  Hex_Digit_Display #(.decimalPoint("false")) hex_digit_display_8 (.value(R4_q));
  assign bit_extender_4_out = {{1{1'b0}}, R4_q_2};  // Bit_Extender bit_extender_4
  xor xor_1 (xor_1_out, j_k_ff_1_q, EndLED);
  Hex_Digit_Display hex_digit_display_9 (.value(Starting_Address[7:4]));  // open: dp
  Hex_Digit_Display hex_digit_display_10 (.value(Starting_Address[3:0]));  // open: dp
  Counter Program_Counter (
    .load(RUN_out), .count(xor_1_out), .clk(CLK), .D(Starting_Address), .Q(Program_Counter_q));  // open: clr, up, carry
  Multiplexer #(.select(2), .width(7)) multiplexer_1 (
    .in0(R1_q), .in1({R2_q_2, R2_q}), .in2({R3_q_2, R3_q}), .in3({R4_q_2, R4_q}), .out(multiplexer_1_out),
    .sel(Rs));
  Multiplexer #(.select(2), .width(7)) multiplexer_2 (
    .in0(R1_q), .in1({R2_q_2, R2_q}), .in2({R3_q_2, R3_q}), .in3({R4_q_2, R4_q}), .out(multiplexer_2_out),
    .sel(Rd));
  Adder #(.width(7)) adder_1 (.a(multiplexer_1_out), .b(multiplexer_2_out), .out(adder_1_out));  // open: cin, cout
  Subtractor #(.width(7)) subtractor_1 (
    .a(multiplexer_2_out), .b(multiplexer_1_out), .out(subtractor_1_out));  // open: bin, bout
  Shifter #(.shift("lr"), .width(7)) shifter_1 (.in(multiplexer_1_out), .\dist (3'b001), .out(shifter_1_out));
  Shifter #(.width(7)) shifter_2 (.in(multiplexer_1_out), .\dist (3'b001), .out(shifter_2_out));
  xor odd_parity_1 (odd_parity_1_out, multiplexer_1_out[0], multiplexer_1_out[1], multiplexer_1_out[2], multiplexer_1_out[3], multiplexer_1_out[4], multiplexer_1_out[5], multiplexer_1_out[6]);
  xnor even_parity_1 (even_parity_1_out, multiplexer_1_out[0], multiplexer_1_out[1], multiplexer_1_out[2], multiplexer_1_out[3], multiplexer_1_out[4], multiplexer_1_out[5], multiplexer_1_out[6]);
  not not_1 (not_1_out, odd_parity_1_out);
  assign bit_extender_5_out = {{1{not_1_out}}, multiplexer_1_out};  // Bit_Extender bit_extender_5
  not not_2 (not_2_out, even_parity_1_out);
  assign bit_extender_6_out = {{1{not_2_out}}, multiplexer_1_out};  // Bit_Extender bit_extender_6
  ROM #(.dataWidth(16)) MicroROM (.addr(Program_Counter_q), .data({OPCODE, EN, Rd, Rs, Rx, IMM}));
  Multiplexer #(.select(3), .width(7)) multiplexer_3 (
    .in0(multiplexer_1_out), .in1(IMM), .in2(adder_1_out), .in3(subtractor_1_out), .in6(shifter_1_out),
    .in7(shifter_2_out), .out(multiplexer_3_out), .sel(OPCODE));  // open: in4, in5
  Multiplexer #(.select(3), .width(8)) multiplexer_4 (
    .in4(bit_extender_5_out), .in5(bit_extender_6_out), .out(multiplexer_4_out), .sel(OPCODE));  // open: in0, in1, in2, in3, in6, in7
  LED led_1 (.in(EndLED));
  nor nor_1 (EndLED, IMM[0], IMM[1], IMM[2], IMM[3], IMM[4], IMM[5], IMM[6], Rx, Rs[0], Rs[1], Rd[0], Rd[1], EN, OPCODE[0], OPCODE[1], OPCODE[2]);

  // Notes on the sheet:
  //   7-bit Data Bus 
  //   Loads Starting Address upon Button Press
  //   Controls running of program
  //   Registers
  //   8-bit Data Bus
  //   Control Unit
  //   ALU
  //   Imm-to-register
  //   Add
  //   Subtract
  //   Logical Shift Right
  //   Logical Shift Left
  //   Odd Parity
  //   Even Parity
  //   Current Address
  //   Register-to-register
  //   contents of MicroROM (hex, n*v repeats v):
  //   3008 1400 5100 13*0 381b 3c0e 7b00 1200 12*0 3004 8080 14*0 3008 d400 dd00 13*0 3007 a080 14*0 3004
  //   f400 f900 13*0 3009 1400 5100 380f 1e00 5b00 5200 dc00 d700
  //   Micro ROM
  //   7-bit Data Bus
endmodule
